// Logisim project arcanoid.circ as structural Verilog: 15 circuits, main circuit main
module main (
);

  wire cdm_16_1_p2, cdm_16_1_p3, cdm_16_1_p5, clk, comparator_1_eq, io_adress_processing_1_mem_2,
       io_adress_processing_1_rd_2, io_adress_processing_1_word_2, io_adress_processing_2_mem_2,
       io_adress_processing_2_rd_2, io_adress_processing_2_word_2, io_adress_processing_3_mem_2,
       io_adress_processing_3_rd_2, io_adress_processing_3_word_2, io_adress_processing_4_mem_2,
       io_adress_processing_4_rd_2, io_adress_processing_4_word_2, kinematic_controller_1_clock_2,
       kinematic_controller_1_rst_2, mem, not_1_out, rd, rst, s_r_ff_1_q, tr1, tr2, triger, upl, word;
  wire [2:0] cdm_16_1_p1, cdm_16_1_p4;
  wire [3:0] divisor_by_10_1_score_low, divisor_by_10_1_score_up, joystick_1_x;
  wire [4:0] ballx, bally, kinematic_controller_1_ballx_2, kinematic_controller_1_bally_2,
       kinematic_controller_1_chip_id, kinematic_controller_1_x_joystick_out, x_joystick;
  wire [5:0] kinematic_controller_1_blockid;
  wire [7:0] cdm_16_1_p1_2, cdm_16_1_p4_2, io_adress_processing_1_wr_out, io_adress_processing_1_wr_out_2,
       pull_resistor_2_node, scor, score;
  wire [7:4] divisor_by_10_1_score_low_2, divisor_by_10_1_score_up_2;
  wire [13:0] pull_resistor_3_node;
  wire [15:0] addr, bit_extender_1_out, cdm_16_1_p10, cdm_16_1_p11, controlled_buffer_2_out, data,
       io_adress_processing_1_addr_2, io_adress_processing_1_out_2, io_adress_processing_2_addr_2,
       io_adress_processing_2_in_2, io_adress_processing_2_out_2, io_adress_processing_3_addr_2,
       io_adress_processing_3_in_2, io_adress_processing_3_out_2, io_adress_processing_4_addr_2,
       io_adress_processing_4_in_2, io_adress_processing_4_out_2, io_adress_processing_5_in_2,
       io_adress_processing_5_out_2, velocity_calculation_1_velocity, velocity_calculation_2_velocity;
  wire [31:0] video_scheme_1_out_8, video_scheme_1_out_9, video_scheme_1_out_10, video_scheme_1_out_11,
       video_scheme_1_out_12, video_scheme_1_out_13, video_scheme_1_out_14, video_scheme_1_out_15,
       video_scheme_1_out_16, video_scheme_1_out_17, video_scheme_1_out_18, video_scheme_1_out_19,
       video_scheme_1_out_20, video_scheme_1_out_21, video_scheme_1_out_22, video_scheme_1_out_23,
       video_scheme_1_out_24, video_scheme_1_out_25, video_scheme_1_out_26, video_scheme_1_out_27,
       video_scheme_1_out_28, video_scheme_1_out_29, video_scheme_1_out_30, video_scheme_1_out_31,
       video_scheme_1_out_32, video_scheme_1_out_33, video_scheme_1_out_34, video_scheme_1_out_35,
       video_scheme_1_out_36, video_scheme_1_out_37, video_scheme_1_out_38, video_scheme_1_out_39;

  // Debugger debugger_1: pin names not known
  Joystick joystick_1 (.x(joystick_1_x));  // open: y
  Clock clock_1 (.out(clk));
  Button button_1 (.out(rst));
  // Probe on cdm_16_1_p2
  S_R_Flip_Flop s_r_ff_1 (.Q(s_r_ff_1_q), .preset(rst), .reset(comparator_1_eq), .en(clk));  // open: S, clk, R, Qn
  Comparator #(.width(5)) comparator_1 (.a({5{1'b1}}), .b(bally), .eq(comparator_1_eq));  // open: gt, lt
  control_bat control_bat_1 (.gamepad_input(joystick_1_x), .clock(clk), .output_x_bat(x_joystick), .restart(rst));
  // CdM_16 cdm_16_1: pin names not known; wires that end beside it: {cdm_16_1_p1_2, ballx, cdm_16_1_p1}, cdm_16_1_p2, cdm_16_1_p3, {cdm_16_1_p4_2, bally, cdm_16_1_p4}, cdm_16_1_p5, mem, rd, word, addr, cdm_16_1_p10, cdm_16_1_p11
  Pull_Resistor pull_resistor_1 (.node(cdm_16_1_p3));
  Transistor #(.\type ("n")) transistor_1 (.in(clk), .out(cdm_16_1_p3), .gate(s_r_ff_1_q));
  // Probe on cdm_16_1_p5
  DotMatrix #(.inputtype("row"), .matrixcols(32), .matrixrows(32)) dotmatrix_1 (
    .row0(video_scheme_1_out_24), .row1(video_scheme_1_out_8), .row2(video_scheme_1_out_25),
    .row3(video_scheme_1_out_9), .row4(video_scheme_1_out_26), .row5(video_scheme_1_out_10),
    .row6(video_scheme_1_out_27), .row7(video_scheme_1_out_11), .row8(video_scheme_1_out_28),
    .row9(video_scheme_1_out_12), .row10(video_scheme_1_out_29), .row11(video_scheme_1_out_13),
    .row12(video_scheme_1_out_30), .row13(video_scheme_1_out_14), .row14(video_scheme_1_out_31),
    .row15(video_scheme_1_out_15), .row16(video_scheme_1_out_32), .row17(video_scheme_1_out_16),
    .row18(video_scheme_1_out_33), .row19(video_scheme_1_out_17), .row20(video_scheme_1_out_34),
    .row21(video_scheme_1_out_18), .row22(video_scheme_1_out_35), .row23(video_scheme_1_out_19),
    .row24(video_scheme_1_out_36), .row25(video_scheme_1_out_20), .row26(video_scheme_1_out_37),
    .row27(video_scheme_1_out_21), .row28(video_scheme_1_out_38), .row29(video_scheme_1_out_22),
    .row30(video_scheme_1_out_39), .row31(video_scheme_1_out_23));
  video_scheme video_scheme_1 (
    .chip_ID(kinematic_controller_1_chip_id), .x_ball(kinematic_controller_1_ballx_2),
    .y_ball(kinematic_controller_1_bally_2), .x_bat(kinematic_controller_1_x_joystick_out),
    .out_24(video_scheme_1_out_24), .out_8(video_scheme_1_out_8), .out_25(video_scheme_1_out_25),
    .out_9(video_scheme_1_out_9), .out_26(video_scheme_1_out_26), .out_10(video_scheme_1_out_10),
    .out_27(video_scheme_1_out_27), .out_11(video_scheme_1_out_11), .out_12(video_scheme_1_out_12),
    .out_13(video_scheme_1_out_13), .out_14(video_scheme_1_out_14), .out_15(video_scheme_1_out_15),
    .out_28(video_scheme_1_out_28), .out_29(video_scheme_1_out_29), .out_30(video_scheme_1_out_30),
    .out_31(video_scheme_1_out_31), .out_16(video_scheme_1_out_16), .out_17(video_scheme_1_out_17),
    .out_18(video_scheme_1_out_18), .out_19(video_scheme_1_out_19), .out_32(video_scheme_1_out_32),
    .out_33(video_scheme_1_out_33), .out_34(video_scheme_1_out_34), .out_35(video_scheme_1_out_35),
    .out_20(video_scheme_1_out_20), .out_21(video_scheme_1_out_21), .out_22(video_scheme_1_out_22),
    .out_23(video_scheme_1_out_23), .out_36(video_scheme_1_out_36), .out_37(video_scheme_1_out_37),
    .out_38(video_scheme_1_out_38), .out_39(video_scheme_1_out_39), .rst(kinematic_controller_1_rst_2),
    .block_ID(kinematic_controller_1_blockid), .clock(kinematic_controller_1_clock_2));
  Register register_1 (.D(pull_resistor_2_node), .en(triger), .Q(score), .clk(clk), .clr(rst));
  Pull_Resistor pull_resistor_2 (.node(pull_resistor_2_node));
  Transistor #(.\type ("n"), .width(8)) transistor_2 (
    .in(io_adress_processing_1_wr_out), .out(pull_resistor_2_node), .gate(triger));
  IO_adress_processing io_adress_processing_1 (
    .addr(addr), .in_2(cdm_16_1_p11), .out(cdm_16_1_p10), .rd(rd), .mem(mem), .word(word),
    .addr_2(io_adress_processing_1_addr_2), .in(io_adress_processing_2_in_2),
    .out_2(io_adress_processing_1_out_2), .rd_2(io_adress_processing_1_rd_2),
    .mem_2(io_adress_processing_1_mem_2), .word_2(io_adress_processing_1_word_2), .trig_to_log(triger),
    .wr_out({io_adress_processing_1_wr_out_2, io_adress_processing_1_wr_out}), .neededAddr(16'hcccc));  // open: rd_in, trig_out_log
  assign bit_extender_1_out = {{11{1'b0}}, x_joystick};  // Bit_Extender bit_extender_1
  kinematic_controller kinematic_controller_1 (
    .clock(clk), .x_joystick(x_joystick), .ballx_2(kinematic_controller_1_ballx_2),
    .bally_2(kinematic_controller_1_bally_2), .x_joystick_out(kinematic_controller_1_x_joystick_out),
    .score(scor), .chip_ID(kinematic_controller_1_chip_id), .rst(rst), .rst_2(kinematic_controller_1_rst_2),
    .clock_2(kinematic_controller_1_clock_2), .blockID(kinematic_controller_1_blockid), .ballx(ballx),
    .bally(bally), .triger(triger), .upl(upl));
  IO_adress_processing io_adress_processing_2 (
    .rd_in(bit_extender_1_out), .addr(io_adress_processing_1_addr_2), .in_2(io_adress_processing_2_in_2),
    .out(io_adress_processing_1_out_2), .rd(io_adress_processing_1_rd_2), .mem(io_adress_processing_1_mem_2),
    .word(io_adress_processing_1_word_2), .addr_2(io_adress_processing_2_addr_2),
    .in(io_adress_processing_3_in_2), .out_2(io_adress_processing_2_out_2),
    .rd_2(io_adress_processing_2_rd_2), .mem_2(io_adress_processing_2_mem_2),
    .word_2(io_adress_processing_2_word_2), .neededAddr(16'hbeef));  // open: trig_to_log, wr_out, trig_out_log
  velocity_calculation velocity_calculation_1 (.clock(clk), .vel_trig(tr1), .velocity(velocity_calculation_1_velocity));
  IO_adress_processing io_adress_processing_3 (
    .rd_in(velocity_calculation_1_velocity), .addr(io_adress_processing_2_addr_2),
    .in_2(io_adress_processing_3_in_2), .out(io_adress_processing_2_out_2), .rd(io_adress_processing_2_rd_2),
    .mem(io_adress_processing_2_mem_2), .word(io_adress_processing_2_word_2),
    .addr_2(io_adress_processing_3_addr_2), .in(io_adress_processing_4_in_2),
    .out_2(io_adress_processing_3_out_2), .rd_2(io_adress_processing_3_rd_2),
    .mem_2(io_adress_processing_3_mem_2), .word_2(io_adress_processing_3_word_2), .trig_out_log(tr1),
    .neededAddr(16'ha000));  // open: trig_to_log, wr_out
  IO_adress_processing io_adress_processing_4 (
    .rd_in(velocity_calculation_2_velocity), .addr(io_adress_processing_3_addr_2),
    .in_2(io_adress_processing_4_in_2), .out(io_adress_processing_3_out_2), .rd(io_adress_processing_3_rd_2),
    .mem(io_adress_processing_3_mem_2), .word(io_adress_processing_3_word_2),
    .addr_2(io_adress_processing_4_addr_2), .in(io_adress_processing_5_in_2),
    .out_2(io_adress_processing_4_out_2), .rd_2(io_adress_processing_4_rd_2),
    .mem_2(io_adress_processing_4_mem_2), .word_2(io_adress_processing_4_word_2), .trig_out_log(tr2),
    .neededAddr(16'ha001));  // open: trig_to_log, wr_out
  velocity_calculation velocity_calculation_2 (.clock(clk), .vel_trig(tr2), .velocity(velocity_calculation_2_velocity));
  IO_adress_processing io_adress_processing_5 (
    .rd_in({pull_resistor_3_node, upl, rst}), .addr(io_adress_processing_4_addr_2),
    .in_2(io_adress_processing_5_in_2), .out(io_adress_processing_4_out_2), .rd(io_adress_processing_4_rd_2),
    .mem(io_adress_processing_4_mem_2), .word(io_adress_processing_4_word_2), .in(controlled_buffer_2_out),
    .out_2(io_adress_processing_5_out_2), .neededAddr(16'ha002));  // open: addr_2, rd_2, mem_2, word_2, trig_to_log, wr_out, trig_out_log
  Pull_Resistor pull_resistor_3 (.node(pull_resistor_3_node));
  Hex_Digit_Display hex_digit_display_1 (.value(divisor_by_10_1_score_up));  // open: dp
  Hex_Digit_Display hex_digit_display_2 (.value(divisor_by_10_1_score_low));  // open: dp
  divisor_by_10 divisor_by_10_1 (
    .data(score), .score_up({divisor_by_10_1_score_up_2, divisor_by_10_1_score_up}),
    .score_low({divisor_by_10_1_score_low_2, divisor_by_10_1_score_low}));
  assign data = not_1_out ? io_adress_processing_5_out_2 : 16'bz;  // Controlled_Buffer controlled_buffer_1
  not not_1 (not_1_out, rd);
  assign controlled_buffer_2_out = rd ? data : 16'bz;  // Controlled_Buffer controlled_buffer_2
  // RAM ram_1: pin names not known; wires that end beside it: addr, word, mem, clk, rd, data
endmodule

module control_bat (
  input  restart,
  input  [3:0] gamepad_input,
  input  clock,
  output [4:0] output_x_bat
);

  wire and_1_out, and_2_out, comparator_1_eq, comparator_1_lt, comparator_2_eq, comparator_3_eq,
       counter_1_carry, not_1_out, not_2_out, not_3_out, not_4_out, or_1_out;
  wire [4:0] counter_2_q;

  Counter #(.width(5), .max('h1f)) counter_1 (
    .count(clock), .carry(counter_1_carry), .clk(clock));  // open: load, D, Q, clr
  and and_1 (and_1_out, comparator_2_eq, not_1_out, not_2_out);
  not not_1 (not_1_out, comparator_1_eq);
  not not_2 (not_2_out, comparator_1_lt);
  and and_2 (and_2_out, comparator_3_eq, not_3_out, comparator_1_lt);
  not not_3 (not_3_out, comparator_1_eq);
  Comparator #(.width(4), .mode("unsigned")) comparator_1 (
    .a(gamepad_input), .b(4'b1000), .eq(comparator_1_eq), .lt(comparator_1_lt));  // open: gt
  or or_1 (or_1_out, comparator_1_eq, and_1_out, and_2_out);
  Counter #(.width(5), .max('h1f)) counter_2 (
    .load(comparator_1_lt), .D(5'b10001), .count(not_4_out), .Q(counter_2_q), .clk(counter_1_carry),
    .clr(restart));  // open: carry
  not not_4 (not_4_out, or_1_out);
  Adder #(.width(5)) adder_1 (.a(5'b10001), .b(counter_2_q), .out(output_x_bat));  // open: cin, cout
  Comparator #(.width(5), .mode("unsigned")) comparator_2 (
    .a(output_x_bat), .b({5{1'b1}}), .eq(comparator_2_eq));  // open: gt, lt
  Comparator #(.width(5), .mode("unsigned")) comparator_3 (
    .a(output_x_bat), .b(5'b00010), .eq(comparator_3_eq));  // open: gt, lt

  // Other names for the same wires on the sheet: rst = restart
endmodule

module video_chip (
  input  [31:0] block_data,
  input  [4:0] chip_ID,
  input  [4:0] x_ball,
  input  [4:0] y_ball,
  input  [4:0] x_bat,
  output [4:0] chip_ID_out,
  output [31:0] out,
  output [4:0] x_ball_out,
  output [4:0] y_ball_out,
  output [4:0] y_bat_out
);

  wire [31:0] decoder_32_inv_1_out, decoder_32_inv_2_out, shifter_1_out, shifter_2_out;

  Pull_Resistor pull_resistor_1 (.node(block_data));
  Adder #(.width(5)) adder_1 (.a(5'b00001), .b(chip_ID), .out(chip_ID_out));  // open: cin, cout
  decoder_32_inv decoder_32_inv_1 (.data(x_ball), .A(y_ball), .B(chip_ID), .out(decoder_32_inv_1_out));
  decoder_32_inv decoder_32_inv_2 (.data(x_bat), .A(chip_ID), .B(5'b11101), .out(decoder_32_inv_2_out));
  Shifter #(.width(32)) shifter_1 (.in(decoder_32_inv_2_out), .\dist (5'b00010), .out(shifter_1_out));
  Shifter #(.width(32)) shifter_2 (.in(decoder_32_inv_2_out), .\dist (5'b00001), .out(shifter_2_out));
  assign out = block_data | decoder_32_inv_1_out | decoder_32_inv_2_out | shifter_1_out | shifter_2_out;  // OR_Gate or_1, 32 bits wide

  assign x_ball_out = x_ball;
  assign y_ball_out = y_ball;
  assign y_bat_out = x_bat;
endmodule

module kinematic_controller (
  input  clock,
  input  triger,
  input  [4:0] ballx,
  input  [4:0] bally,
  input  [4:0] x_joystick,
  input  upl,
  input  rst,
  output clock_2,
  output [4:0] chip_ID,
  output [4:0] ballx_2,
  output [4:0] bally_2,
  output [4:0] x_joystick_out,
  output rst_2,
  output [7:0] score,
  output [5:0] blockID
);

  Counter #(.width(6), .max('h20)) counter_1 (.count(triger), .carry(upl), .clk(clock));  // open: load, D, Q, clr
  Pull_Resistor pull_resistor_1 (.node(upl));
  or or_1 (rst_2, rst, upl);
  triger_of_deleting triger_of_deleting_1 (.ballx(ballx), .bally(bally), .blockID(blockID), .triger(triger));

  assign ballx_2 = ballx;
  assign bally_2 = bally;
  assign chip_ID = {5{1'b0}};
  assign clock_2 = clock;
  assign score = 8'h56;
  assign x_joystick_out = x_joystick;
  // also tied to GND on the sheet: upl

  // Other names for the same wires on the sheet: clk = clock

  // Notes on the sheet:
  //   IO
endmodule

module decoder_32_inv (
  input  [4:0] data,
  input  [4:0] A,
  input  [4:0] B,
  output [31:0] out
);

  wire comparator_1_eq;

  Comparator #(.width(5)) comparator_1 (.a(A), .b(B), .eq(comparator_1_eq));  // open: gt, lt
  Decoder #(.select(5), .disabled(0)) decoder_1 (
    .out0(out[31]), .out1(out[30]), .out2(out[29]), .out3(out[28]), .out4(out[27]), .out5(out[26]),
    .out6(out[25]), .out7(out[24]), .out8(out[23]), .out9(out[22]), .out10(out[21]), .out11(out[20]),
    .out12(out[19]), .out13(out[18]), .out14(out[17]), .out15(out[16]), .out16(out[15]), .out17(out[14]),
    .out18(out[13]), .out19(out[12]), .out20(out[11]), .out21(out[10]), .out22(out[9]), .out23(out[8]),
    .out24(out[7]), .out25(out[6]), .out26(out[5]), .out27(out[4]), .out28(out[3]), .out29(out[2]),
    .out30(out[1]), .out31(out[0]), .sel(data), .en(comparator_1_eq));
endmodule

module video_scheme (
  input  [4:0] chip_ID,
  input  [4:0] x_ball,
  input  [4:0] y_ball,
  input  [4:0] x_bat,
  input  rst,
  input  clock,
  input  [5:0] block_ID,
  output [31:0] out_8,
  output [31:0] out_9,
  output [31:0] out_10,
  output [31:0] out_11,
  output [31:0] out_12,
  output [31:0] out_13,
  output [31:0] out_14,
  output [31:0] out_15,
  output [31:0] out_16,
  output [31:0] out_17,
  output [31:0] out_18,
  output [31:0] out_19,
  output [31:0] out_20,
  output [31:0] out_21,
  output [31:0] out_22,
  output [31:0] out_23,
  output [31:0] out_24,
  output [31:0] out_25,
  output [31:0] out_26,
  output [31:0] out_27,
  output [31:0] out_28,
  output [31:0] out_29,
  output [31:0] out_30,
  output [31:0] out_31,
  output [31:0] out_32,
  output [31:0] out_33,
  output [31:0] out_34,
  output [31:0] out_35,
  output [31:0] out_36,
  output [31:0] out_37,
  output [31:0] out_38,
  output [31:0] out_39
);

  wire and_1_out, comparator_1_eq, det;
  wire [2:0] multiplexer_3_out;
  wire [4:0] video_chip_1_chip_id_out, video_chip_1_x_ball_out, video_chip_1_y_ball_out,
       video_chip_1_y_bat_out, video_chip_2_chip_id_out, video_chip_2_x_ball_out, video_chip_2_y_ball_out,
       video_chip_2_y_bat_out, video_chip_3_chip_id_out, video_chip_3_x_ball_out, video_chip_3_y_ball_out,
       video_chip_3_y_bat_out, video_chip_4_chip_id_out, video_chip_4_x_ball_out, video_chip_4_y_ball_out,
       video_chip_4_y_bat_out, video_chip_5_chip_id_out, video_chip_5_x_ball_out, video_chip_5_y_ball_out,
       video_chip_5_y_bat_out, video_chip_6_chip_id_out, video_chip_6_x_ball_out, video_chip_6_y_ball_out,
       video_chip_6_y_bat_out, video_chip_7_chip_id_out, video_chip_7_x_ball_out, video_chip_7_y_ball_out,
       video_chip_7_y_bat_out, video_chip_8_chip_id_out, video_chip_8_x_ball_out, video_chip_8_y_ball_out,
       video_chip_8_y_bat_out, video_chip_9_chip_id_out, video_chip_9_x_ball_out, video_chip_9_y_ball_out,
       video_chip_9_y_bat_out, video_chip_10_chip_id_out, video_chip_10_x_ball_out, video_chip_10_y_ball_out,
       video_chip_10_y_bat_out, video_chip_11_chip_id_out, video_chip_11_x_ball_out,
       video_chip_11_y_ball_out, video_chip_11_y_bat_out, video_chip_12_chip_id_out,
       video_chip_12_x_ball_out, video_chip_12_y_ball_out, video_chip_12_y_bat_out,
       video_chip_13_chip_id_out, video_chip_13_x_ball_out, video_chip_13_y_ball_out,
       video_chip_13_y_bat_out, video_chip_14_chip_id_out, video_chip_14_x_ball_out,
       video_chip_14_y_ball_out, video_chip_14_y_bat_out, video_chip_15_chip_id_out,
       video_chip_15_x_ball_out, video_chip_15_y_ball_out, video_chip_15_y_bat_out,
       video_chip_16_chip_id_out, video_chip_16_x_ball_out, video_chip_16_y_ball_out,
       video_chip_16_y_bat_out, video_chip_17_chip_id_out, video_chip_17_x_ball_out,
       video_chip_17_y_ball_out, video_chip_17_y_bat_out, video_chip_18_chip_id_out,
       video_chip_18_x_ball_out, video_chip_18_y_ball_out, video_chip_18_y_bat_out,
       video_chip_19_chip_id_out, video_chip_19_x_ball_out, video_chip_19_y_ball_out,
       video_chip_19_y_bat_out, video_chip_20_chip_id_out, video_chip_20_x_ball_out,
       video_chip_20_y_ball_out, video_chip_20_y_bat_out, video_chip_21_chip_id_out,
       video_chip_21_x_ball_out, video_chip_21_y_ball_out, video_chip_21_y_bat_out,
       video_chip_22_chip_id_out, video_chip_22_x_ball_out, video_chip_22_y_ball_out,
       video_chip_22_y_bat_out, video_chip_23_chip_id_out, video_chip_23_x_ball_out,
       video_chip_23_y_ball_out, video_chip_23_y_bat_out, video_chip_24_chip_id_out,
       video_chip_24_x_ball_out, video_chip_24_y_ball_out, video_chip_24_y_bat_out,
       video_chip_25_chip_id_out, video_chip_25_x_ball_out, video_chip_25_y_ball_out,
       video_chip_25_y_bat_out, video_chip_26_chip_id_out, video_chip_26_x_ball_out,
       video_chip_26_y_ball_out, video_chip_26_y_bat_out, video_chip_27_chip_id_out,
       video_chip_27_x_ball_out, video_chip_27_y_ball_out, video_chip_27_y_bat_out,
       video_chip_28_chip_id_out, video_chip_28_x_ball_out, video_chip_28_y_ball_out,
       video_chip_28_y_bat_out, video_chip_29_chip_id_out, video_chip_29_x_ball_out,
       video_chip_29_y_ball_out, video_chip_29_y_bat_out, video_chip_30_chip_id_out,
       video_chip_30_x_ball_out, video_chip_30_y_ball_out, video_chip_30_y_bat_out,
       video_chip_31_chip_id_out, video_chip_31_x_ball_out, video_chip_31_y_ball_out, video_chip_31_y_bat_out;
  wire [5:0] adder_1_out, demultiplexer_1_out1, demultiplexer_1_out2, demultiplexer_1_out3,
       demultiplexer_1_out4, divider_1_out, divider_1_rem, multiplexer_1_out, multiplexer_2_out, or_1_out,
       res1, res2;
  wire [5:3] multiplexer_3_out_2;
  wire [31:0] _1, _2, _4, _5, _7, _8, _10, _11;

  Comparator #(.width(6)) comparator_1 (.a(res2), .b({6{1'b0}}), .eq(comparator_1_eq));  // open: gt, lt
  Adder #(.width(6)) adder_1 (.a(res1), .b(6'b000001), .out(adder_1_out));  // open: cin, cout
  Multiplexer #(.width(6), .enable("false")) multiplexer_1 (
    .in0(res2), .in1(6'b001000), .out(multiplexer_1_out), .sel(comparator_1_eq));
  Multiplexer #(.width(6), .enable("false")) multiplexer_2 (
    .in0(res1), .in1(adder_1_out), .out(multiplexer_2_out), .sel(det));
  video_chip video_chip_1 (
    .chip_ID(chip_ID), .x_ball(x_ball), .y_ball(y_ball), .x_bat(x_bat),
    .chip_ID_out(video_chip_1_chip_id_out), .out(out_24), .x_ball_out(video_chip_1_x_ball_out),
    .y_ball_out(video_chip_1_y_ball_out), .y_bat_out(video_chip_1_y_bat_out));  // open: block_data
  Divider #(.width(6)) divider_1 (
    .a(block_ID), .b(6'b001000), .out(divider_1_out), .rem(divider_1_rem));  // open: upper
  Demultiplexer #(.select(3), .width(6), .enable("false")) demultiplexer_1 (
    .out1(demultiplexer_1_out1), .out2(demultiplexer_1_out2), .out3(demultiplexer_1_out3),
    .out4(demultiplexer_1_out4), .in(multiplexer_1_out), .sel(multiplexer_3_out));  // open: out0, out5, out6, out7
  Multiplexer #(.width(6), .enable("false")) multiplexer_3 (
    .in0(multiplexer_2_out), .in1(res1), .out({multiplexer_3_out_2, multiplexer_3_out}), .sel(and_1_out));
  and and_1 (and_1_out, comparator_1_eq, det);
  video_chip video_chip_2 (
    .chip_ID(video_chip_3_chip_id_out), .x_ball(video_chip_3_x_ball_out), .y_ball(video_chip_3_y_ball_out),
    .x_bat(video_chip_3_y_bat_out), .chip_ID_out(video_chip_2_chip_id_out), .out(out_25),
    .x_ball_out(video_chip_2_x_ball_out), .y_ball_out(video_chip_2_y_ball_out),
    .y_bat_out(video_chip_2_y_bat_out), .block_data(_2));
  video_chip video_chip_3 (
    .chip_ID(video_chip_1_chip_id_out), .x_ball(video_chip_1_x_ball_out), .y_ball(video_chip_1_y_ball_out),
    .x_bat(video_chip_1_y_bat_out), .chip_ID_out(video_chip_3_chip_id_out), .out(out_8),
    .x_ball_out(video_chip_3_x_ball_out), .y_ball_out(video_chip_3_y_ball_out),
    .y_bat_out(video_chip_3_y_bat_out), .block_data(_1));
  assign or_1_out = divider_1_out | divider_1_rem;  // OR_Gate or_1, 6 bits wide
  video_chip video_chip_4 (
    .chip_ID(video_chip_2_chip_id_out), .x_ball(video_chip_2_x_ball_out), .y_ball(video_chip_2_y_ball_out),
    .x_bat(video_chip_2_y_bat_out), .chip_ID_out(video_chip_4_chip_id_out), .out(out_9),
    .x_ball_out(video_chip_4_x_ball_out), .y_ball_out(video_chip_4_y_ball_out),
    .y_bat_out(video_chip_4_y_bat_out));  // open: block_data
  video_chip video_chip_5 (
    .chip_ID(video_chip_4_chip_id_out), .x_ball(video_chip_4_x_ball_out), .y_ball(video_chip_4_y_ball_out),
    .x_bat(video_chip_4_y_bat_out), .chip_ID_out(video_chip_5_chip_id_out), .out(out_26),
    .x_ball_out(video_chip_5_x_ball_out), .y_ball_out(video_chip_5_y_ball_out),
    .y_bat_out(video_chip_5_y_bat_out), .block_data(_4));
  Comparator #(.width(6)) comparator_2 (.a(or_1_out), .b({6{1'b0}}), .gt(det));  // open: eq, lt
  video_chip video_chip_6 (
    .chip_ID(video_chip_5_chip_id_out), .x_ball(video_chip_5_x_ball_out), .y_ball(video_chip_5_y_ball_out),
    .x_bat(video_chip_5_y_bat_out), .chip_ID_out(video_chip_6_chip_id_out), .out(out_10),
    .x_ball_out(video_chip_6_x_ball_out), .y_ball_out(video_chip_6_y_ball_out),
    .y_bat_out(video_chip_6_y_bat_out), .block_data(_5));
  video_chip video_chip_7 (
    .chip_ID(video_chip_6_chip_id_out), .x_ball(video_chip_6_x_ball_out), .y_ball(video_chip_6_y_ball_out),
    .x_bat(video_chip_6_y_bat_out), .chip_ID_out(video_chip_7_chip_id_out), .out(out_27),
    .x_ball_out(video_chip_7_x_ball_out), .y_ball_out(video_chip_7_y_ball_out),
    .y_bat_out(video_chip_7_y_bat_out));  // open: block_data
  Transistor #(.\type ("n"), .width(6)) transistor_1 (.in(divider_1_out), .out(res1), .gate(det));
  Transistor #(.\type ("n"), .width(6)) transistor_2 (.in(divider_1_rem), .out(res2), .gate(det));
  video_chip video_chip_8 (
    .chip_ID(video_chip_9_chip_id_out), .x_ball(video_chip_9_x_ball_out), .y_ball(video_chip_9_y_ball_out),
    .x_bat(video_chip_9_y_bat_out), .chip_ID_out(video_chip_8_chip_id_out), .out(out_28),
    .x_ball_out(video_chip_8_x_ball_out), .y_ball_out(video_chip_8_y_ball_out),
    .y_bat_out(video_chip_8_y_bat_out), .block_data(_8));
  video_chip video_chip_9 (
    .chip_ID(video_chip_7_chip_id_out), .x_ball(video_chip_7_x_ball_out), .y_ball(video_chip_7_y_ball_out),
    .x_bat(video_chip_7_y_bat_out), .chip_ID_out(video_chip_9_chip_id_out), .out(out_11),
    .x_ball_out(video_chip_9_x_ball_out), .y_ball_out(video_chip_9_y_ball_out),
    .y_bat_out(video_chip_9_y_bat_out), .block_data(_7));
  video_chip video_chip_10 (
    .chip_ID(video_chip_8_chip_id_out), .x_ball(video_chip_8_x_ball_out), .y_ball(video_chip_8_y_ball_out),
    .x_bat(video_chip_8_y_bat_out), .chip_ID_out(video_chip_10_chip_id_out), .out(out_12),
    .x_ball_out(video_chip_10_x_ball_out), .y_ball_out(video_chip_10_y_ball_out),
    .y_bat_out(video_chip_10_y_bat_out));  // open: block_data
  video_chip video_chip_11 (
    .chip_ID(video_chip_10_chip_id_out), .x_ball(video_chip_10_x_ball_out),
    .y_ball(video_chip_10_y_ball_out), .x_bat(video_chip_10_y_bat_out),
    .chip_ID_out(video_chip_11_chip_id_out), .out(out_29), .x_ball_out(video_chip_11_x_ball_out),
    .y_ball_out(video_chip_11_y_ball_out), .y_bat_out(video_chip_11_y_bat_out), .block_data(_10));
  blocks_detector blocks_detector_1 (
    .rst(rst), .chip_ID(5'b00010), .clk(clock), .block_ID_1_8(demultiplexer_1_out1), .up(_1), .down(_2));
  blocks_detector blocks_detector_2 (
    .rst(rst), .chip_ID(5'b00101), .clk(clock), .block_ID_1_8(demultiplexer_1_out2), .up(_4), .down(_5));
  blocks_detector blocks_detector_3 (
    .rst(rst), .chip_ID(5'b01000), .clk(clock), .block_ID_1_8(demultiplexer_1_out3), .up(_7), .down(_8));
  blocks_detector blocks_detector_4 (
    .rst(rst), .chip_ID(5'b01011), .clk(clock), .block_ID_1_8(demultiplexer_1_out4), .up(_10), .down(_11));
  video_chip video_chip_12 (
    .chip_ID(video_chip_11_chip_id_out), .x_ball(video_chip_11_x_ball_out),
    .y_ball(video_chip_11_y_ball_out), .x_bat(video_chip_11_y_bat_out),
    .chip_ID_out(video_chip_12_chip_id_out), .out(out_13), .x_ball_out(video_chip_12_x_ball_out),
    .y_ball_out(video_chip_12_y_ball_out), .y_bat_out(video_chip_12_y_bat_out), .block_data(_11));
  video_chip video_chip_13 (
    .chip_ID(video_chip_12_chip_id_out), .x_ball(video_chip_12_x_ball_out),
    .y_ball(video_chip_12_y_ball_out), .x_bat(video_chip_12_y_bat_out),
    .chip_ID_out(video_chip_13_chip_id_out), .out(out_30), .x_ball_out(video_chip_13_x_ball_out),
    .y_ball_out(video_chip_13_y_ball_out), .y_bat_out(video_chip_13_y_bat_out));  // open: block_data
  video_chip video_chip_14 (
    .chip_ID(video_chip_13_chip_id_out), .x_ball(video_chip_13_x_ball_out),
    .y_ball(video_chip_13_y_ball_out), .x_bat(video_chip_13_y_bat_out),
    .chip_ID_out(video_chip_14_chip_id_out), .out(out_14), .x_ball_out(video_chip_14_x_ball_out),
    .y_ball_out(video_chip_14_y_ball_out), .y_bat_out(video_chip_14_y_bat_out));  // open: block_data
  video_chip video_chip_15 (
    .chip_ID(video_chip_14_chip_id_out), .x_ball(video_chip_14_x_ball_out),
    .y_ball(video_chip_14_y_ball_out), .x_bat(video_chip_14_y_bat_out),
    .chip_ID_out(video_chip_15_chip_id_out), .out(out_31), .x_ball_out(video_chip_15_x_ball_out),
    .y_ball_out(video_chip_15_y_ball_out), .y_bat_out(video_chip_15_y_bat_out));  // open: block_data
  video_chip video_chip_16 (
    .chip_ID(video_chip_17_chip_id_out), .x_ball(video_chip_17_x_ball_out),
    .y_ball(video_chip_17_y_ball_out), .x_bat(video_chip_17_y_bat_out),
    .chip_ID_out(video_chip_16_chip_id_out), .out(out_32), .x_ball_out(video_chip_16_x_ball_out),
    .y_ball_out(video_chip_16_y_ball_out), .y_bat_out(video_chip_16_y_bat_out));  // open: block_data
  video_chip video_chip_17 (
    .chip_ID(video_chip_15_chip_id_out), .x_ball(video_chip_15_x_ball_out),
    .y_ball(video_chip_15_y_ball_out), .x_bat(video_chip_15_y_bat_out),
    .chip_ID_out(video_chip_17_chip_id_out), .out(out_15), .x_ball_out(video_chip_17_x_ball_out),
    .y_ball_out(video_chip_17_y_ball_out), .y_bat_out(video_chip_17_y_bat_out));  // open: block_data
  video_chip video_chip_18 (
    .chip_ID(video_chip_16_chip_id_out), .x_ball(video_chip_16_x_ball_out),
    .y_ball(video_chip_16_y_ball_out), .x_bat(video_chip_16_y_bat_out),
    .chip_ID_out(video_chip_18_chip_id_out), .out(out_16), .x_ball_out(video_chip_18_x_ball_out),
    .y_ball_out(video_chip_18_y_ball_out), .y_bat_out(video_chip_18_y_bat_out));  // open: block_data
  video_chip video_chip_19 (
    .chip_ID(video_chip_18_chip_id_out), .x_ball(video_chip_18_x_ball_out),
    .y_ball(video_chip_18_y_ball_out), .x_bat(video_chip_18_y_bat_out),
    .chip_ID_out(video_chip_19_chip_id_out), .out(out_33), .x_ball_out(video_chip_19_x_ball_out),
    .y_ball_out(video_chip_19_y_ball_out), .y_bat_out(video_chip_19_y_bat_out));  // open: block_data
  video_chip video_chip_20 (
    .chip_ID(video_chip_21_chip_id_out), .x_ball(video_chip_21_x_ball_out),
    .y_ball(video_chip_21_y_ball_out), .x_bat(video_chip_21_y_bat_out),
    .chip_ID_out(video_chip_20_chip_id_out), .out(out_34), .x_ball_out(video_chip_20_x_ball_out),
    .y_ball_out(video_chip_20_y_ball_out), .y_bat_out(video_chip_20_y_bat_out));  // open: block_data
  video_chip video_chip_21 (
    .chip_ID(video_chip_19_chip_id_out), .x_ball(video_chip_19_x_ball_out),
    .y_ball(video_chip_19_y_ball_out), .x_bat(video_chip_19_y_bat_out),
    .chip_ID_out(video_chip_21_chip_id_out), .out(out_17), .x_ball_out(video_chip_21_x_ball_out),
    .y_ball_out(video_chip_21_y_ball_out), .y_bat_out(video_chip_21_y_bat_out));  // open: block_data
  video_chip video_chip_22 (
    .chip_ID(video_chip_23_chip_id_out), .x_ball(video_chip_23_x_ball_out),
    .y_ball(video_chip_23_y_ball_out), .x_bat(video_chip_23_y_bat_out),
    .chip_ID_out(video_chip_22_chip_id_out), .out(out_35), .x_ball_out(video_chip_22_x_ball_out),
    .y_ball_out(video_chip_22_y_ball_out), .y_bat_out(video_chip_22_y_bat_out));  // open: block_data
  video_chip video_chip_23 (
    .chip_ID(video_chip_20_chip_id_out), .x_ball(video_chip_20_x_ball_out),
    .y_ball(video_chip_20_y_ball_out), .x_bat(video_chip_20_y_bat_out),
    .chip_ID_out(video_chip_23_chip_id_out), .out(out_18), .x_ball_out(video_chip_23_x_ball_out),
    .y_ball_out(video_chip_23_y_ball_out), .y_bat_out(video_chip_23_y_bat_out));  // open: block_data
  video_chip video_chip_24 (
    .chip_ID(video_chip_25_chip_id_out), .x_ball(video_chip_25_x_ball_out),
    .y_ball(video_chip_25_y_ball_out), .x_bat(video_chip_25_y_bat_out),
    .chip_ID_out(video_chip_24_chip_id_out), .out(out_36), .x_ball_out(video_chip_24_x_ball_out),
    .y_ball_out(video_chip_24_y_ball_out), .y_bat_out(video_chip_24_y_bat_out));  // open: block_data
  video_chip video_chip_25 (
    .chip_ID(video_chip_22_chip_id_out), .x_ball(video_chip_22_x_ball_out),
    .y_ball(video_chip_22_y_ball_out), .x_bat(video_chip_22_y_bat_out),
    .chip_ID_out(video_chip_25_chip_id_out), .out(out_19), .x_ball_out(video_chip_25_x_ball_out),
    .y_ball_out(video_chip_25_y_ball_out), .y_bat_out(video_chip_25_y_bat_out));  // open: block_data
  video_chip video_chip_26 (
    .chip_ID(video_chip_24_chip_id_out), .x_ball(video_chip_24_x_ball_out),
    .y_ball(video_chip_24_y_ball_out), .x_bat(video_chip_24_y_bat_out),
    .chip_ID_out(video_chip_26_chip_id_out), .out(out_20), .x_ball_out(video_chip_26_x_ball_out),
    .y_ball_out(video_chip_26_y_ball_out), .y_bat_out(video_chip_26_y_bat_out));  // open: block_data
  video_chip video_chip_27 (
    .chip_ID(video_chip_26_chip_id_out), .x_ball(video_chip_26_x_ball_out),
    .y_ball(video_chip_26_y_ball_out), .x_bat(video_chip_26_y_bat_out),
    .chip_ID_out(video_chip_27_chip_id_out), .out(out_37), .x_ball_out(video_chip_27_x_ball_out),
    .y_ball_out(video_chip_27_y_ball_out), .y_bat_out(video_chip_27_y_bat_out));  // open: block_data
  video_chip video_chip_28 (
    .chip_ID(video_chip_27_chip_id_out), .x_ball(video_chip_27_x_ball_out),
    .y_ball(video_chip_27_y_ball_out), .x_bat(video_chip_27_y_bat_out),
    .chip_ID_out(video_chip_28_chip_id_out), .out(out_21), .x_ball_out(video_chip_28_x_ball_out),
    .y_ball_out(video_chip_28_y_ball_out), .y_bat_out(video_chip_28_y_bat_out));  // open: block_data
  video_chip video_chip_29 (
    .chip_ID(video_chip_28_chip_id_out), .x_ball(video_chip_28_x_ball_out),
    .y_ball(video_chip_28_y_ball_out), .x_bat(video_chip_28_y_bat_out),
    .chip_ID_out(video_chip_29_chip_id_out), .out(out_38), .x_ball_out(video_chip_29_x_ball_out),
    .y_ball_out(video_chip_29_y_ball_out), .y_bat_out(video_chip_29_y_bat_out));  // open: block_data
  video_chip video_chip_30 (
    .chip_ID(video_chip_29_chip_id_out), .x_ball(video_chip_29_x_ball_out),
    .y_ball(video_chip_29_y_ball_out), .x_bat(video_chip_29_y_bat_out),
    .chip_ID_out(video_chip_30_chip_id_out), .out(out_22), .x_ball_out(video_chip_30_x_ball_out),
    .y_ball_out(video_chip_30_y_ball_out), .y_bat_out(video_chip_30_y_bat_out));  // open: block_data
  video_chip video_chip_31 (
    .chip_ID(video_chip_30_chip_id_out), .x_ball(video_chip_30_x_ball_out),
    .y_ball(video_chip_30_y_ball_out), .x_bat(video_chip_30_y_bat_out),
    .chip_ID_out(video_chip_31_chip_id_out), .out(out_39), .x_ball_out(video_chip_31_x_ball_out),
    .y_ball_out(video_chip_31_y_ball_out), .y_bat_out(video_chip_31_y_bat_out));  // open: block_data
  video_chip video_chip_32 (
    .chip_ID(video_chip_31_chip_id_out), .x_ball(video_chip_31_x_ball_out),
    .y_ball(video_chip_31_y_ball_out), .x_bat(video_chip_31_y_bat_out), .out(out_23));  // open: chip_ID_out, x_ball_out, y_ball_out, y_bat_out, block_data

  // Other names for the same wires on the sheet: clk = clock
endmodule

module divisor_by_10 (
  input  [7:0] data,
  output [7:0] score_up,
  output [7:0] score_low
);

  Divider divider_1 (.a(data), .b(8'ha), .out(score_up), .rem(score_low));  // open: upper
endmodule

module blocks_detector (
  input  rst,
  input  [4:0] chip_ID,
  input  clk,
  input  [5:0] block_ID_1_8,
  output [31:0] up,
  output [31:0] down
);

  wire min_comparator_1_result, min_comparator_2_result, min_comparator_3_result, min_comparator_4_result,
       min_comparator_5_result, min_comparator_6_result, min_comparator_7_result, min_comparator_8_result,
       s_r_ff_1_q, s_r_ff_2_q, s_r_ff_3_q, s_r_ff_4_q, s_r_ff_5_q, s_r_ff_6_q, s_r_ff_7_q, s_r_ff_8_q;
  wire [4:0] block_paint_1_shift_2, block_paint_1_string_2, block_paint_2_string_2, block_paint_3_shift_2,
       block_paint_3_string_2, block_paint_4_string_2, block_paint_5_shift_2, block_paint_5_string_2,
       block_paint_6_string_2, block_paint_7_shift_2, block_paint_7_string_2, block_paint_8_string_2,
       block_paint_9_shift_2, block_paint_9_string_2, block_paint_10_string_2, block_paint_11_shift_2,
       block_paint_11_string_2, block_paint_12_string_2, block_paint_13_shift_2, block_paint_13_string_2,
       block_paint_14_string_2, chip, ID1;
  wire [5:0] min_comparator_1_first_2, min_comparator_1_second_2, min_comparator_2_first_2,
       min_comparator_2_second_2, min_comparator_3_first_2, min_comparator_3_second_2,
       min_comparator_4_first_2, min_comparator_4_second_2, min_comparator_5_first_2,
       min_comparator_5_second_2, min_comparator_6_first_2, min_comparator_6_second_2,
       min_comparator_7_first_2, min_comparator_7_second_2;
  wire [31:0] block_paint_1_t_string_2, block_paint_2_t_string_2, block_paint_3_t_string_2,
       block_paint_4_t_string_2, block_paint_5_t_string_2, block_paint_6_t_string_2,
       block_paint_7_t_string_2, block_paint_8_t_string_2, block_paint_9_t_string_2,
       block_paint_10_t_string_2, block_paint_11_t_string_2, block_paint_12_t_string_2,
       block_paint_13_t_string_2, block_paint_14_t_string_2, block_paint_15_t_string_2,
       block_paint_16_t_string_2;

  Subtractor #(.width(5)) subtractor_1 (.a(chip_ID), .b(5'b00001), .out(ID1));  // open: bin, bout
  S_R_Flip_Flop s_r_ff_1 (
    .Q(s_r_ff_1_q), .preset(rst), .reset(min_comparator_1_result), .en(clk));  // open: S, clk, R, Qn
  min_comparator min_comparator_1 (
    .first(block_ID_1_8), .second(6'b000001), .result(min_comparator_1_result),
    .second_2(min_comparator_1_second_2), .first_2(min_comparator_1_first_2));
  block_paint block_paint_1 (
    .data(s_r_ff_1_q), .\string (ID1), .t_string(chip), .shift(5'b00010), .shift_2(block_paint_1_shift_2),
    .t_string_2(block_paint_1_t_string_2), .string_2(block_paint_1_string_2));
  block_paint block_paint_2 (
    .data(s_r_ff_1_q), .\string (chip_ID), .t_string(chip), .shift(5'b00010),
    .t_string_2(block_paint_2_t_string_2), .string_2(block_paint_2_string_2));  // open: shift_2
  S_R_Flip_Flop s_r_ff_2 (
    .Q(s_r_ff_2_q), .preset(rst), .reset(min_comparator_2_result), .en(clk));  // open: S, clk, R, Qn
  min_comparator min_comparator_2 (
    .first(min_comparator_1_first_2), .second(min_comparator_1_second_2), .result(min_comparator_2_result),
    .second_2(min_comparator_2_second_2), .first_2(min_comparator_2_first_2));
  block_paint block_paint_3 (
    .data(s_r_ff_2_q), .\string (block_paint_1_string_2), .t_string(chip), .shift(block_paint_1_shift_2),
    .shift_2(block_paint_3_shift_2), .t_string_2(block_paint_3_t_string_2), .string_2(block_paint_3_string_2));
  block_paint block_paint_4 (
    .data(s_r_ff_2_q), .\string (block_paint_2_string_2), .t_string(chip), .shift(block_paint_1_shift_2),
    .t_string_2(block_paint_4_t_string_2), .string_2(block_paint_4_string_2));  // open: shift_2
  S_R_Flip_Flop s_r_ff_3 (
    .Q(s_r_ff_3_q), .preset(rst), .reset(min_comparator_3_result), .en(clk));  // open: S, clk, R, Qn
  min_comparator min_comparator_3 (
    .first(min_comparator_2_first_2), .second(min_comparator_2_second_2), .result(min_comparator_3_result),
    .second_2(min_comparator_3_second_2), .first_2(min_comparator_3_first_2));
  block_paint block_paint_5 (
    .data(s_r_ff_3_q), .\string (block_paint_3_string_2), .t_string(chip), .shift(block_paint_3_shift_2),
    .shift_2(block_paint_5_shift_2), .t_string_2(block_paint_5_t_string_2), .string_2(block_paint_5_string_2));
  block_paint block_paint_6 (
    .data(s_r_ff_3_q), .\string (block_paint_4_string_2), .t_string(chip), .shift(block_paint_3_shift_2),
    .t_string_2(block_paint_6_t_string_2), .string_2(block_paint_6_string_2));  // open: shift_2
  S_R_Flip_Flop s_r_ff_4 (
    .Q(s_r_ff_4_q), .preset(rst), .reset(min_comparator_4_result), .en(clk));  // open: S, clk, R, Qn
  min_comparator min_comparator_4 (
    .first(min_comparator_3_first_2), .second(min_comparator_3_second_2), .result(min_comparator_4_result),
    .second_2(min_comparator_4_second_2), .first_2(min_comparator_4_first_2));
  block_paint block_paint_7 (
    .data(s_r_ff_4_q), .\string (block_paint_5_string_2), .t_string(chip), .shift(block_paint_5_shift_2),
    .shift_2(block_paint_7_shift_2), .t_string_2(block_paint_7_t_string_2), .string_2(block_paint_7_string_2));
  block_paint block_paint_8 (
    .data(s_r_ff_4_q), .\string (block_paint_6_string_2), .t_string(chip), .shift(block_paint_5_shift_2),
    .t_string_2(block_paint_8_t_string_2), .string_2(block_paint_8_string_2));  // open: shift_2
  assign up = block_paint_1_t_string_2 | block_paint_3_t_string_2 | block_paint_5_t_string_2 | block_paint_7_t_string_2 | block_paint_9_t_string_2 | block_paint_11_t_string_2 | block_paint_13_t_string_2 | block_paint_15_t_string_2;  // OR_Gate or_1, 32 bits wide
  S_R_Flip_Flop s_r_ff_5 (
    .Q(s_r_ff_5_q), .preset(rst), .reset(min_comparator_5_result), .en(clk));  // open: S, clk, R, Qn
  min_comparator min_comparator_5 (
    .first(min_comparator_4_first_2), .second(min_comparator_4_second_2), .result(min_comparator_5_result),
    .second_2(min_comparator_5_second_2), .first_2(min_comparator_5_first_2));
  assign down = block_paint_2_t_string_2 | block_paint_4_t_string_2 | block_paint_6_t_string_2 | block_paint_8_t_string_2 | block_paint_10_t_string_2 | block_paint_12_t_string_2 | block_paint_14_t_string_2 | block_paint_16_t_string_2;  // OR_Gate or_2, 32 bits wide
  block_paint block_paint_9 (
    .data(s_r_ff_5_q), .\string (block_paint_7_string_2), .t_string(chip), .shift(block_paint_7_shift_2),
    .shift_2(block_paint_9_shift_2), .t_string_2(block_paint_9_t_string_2), .string_2(block_paint_9_string_2));
  block_paint block_paint_10 (
    .data(s_r_ff_5_q), .\string (block_paint_8_string_2), .t_string(chip), .shift(block_paint_7_shift_2),
    .t_string_2(block_paint_10_t_string_2), .string_2(block_paint_10_string_2));  // open: shift_2
  S_R_Flip_Flop s_r_ff_6 (
    .Q(s_r_ff_6_q), .preset(rst), .reset(min_comparator_6_result), .en(clk));  // open: S, clk, R, Qn
  min_comparator min_comparator_6 (
    .first(min_comparator_5_first_2), .second(min_comparator_5_second_2), .result(min_comparator_6_result),
    .second_2(min_comparator_6_second_2), .first_2(min_comparator_6_first_2));
  block_paint block_paint_11 (
    .data(s_r_ff_6_q), .\string (block_paint_9_string_2), .t_string(chip), .shift(block_paint_9_shift_2),
    .shift_2(block_paint_11_shift_2), .t_string_2(block_paint_11_t_string_2),
    .string_2(block_paint_11_string_2));
  block_paint block_paint_12 (
    .data(s_r_ff_6_q), .\string (block_paint_10_string_2), .t_string(chip), .shift(block_paint_9_shift_2),
    .t_string_2(block_paint_12_t_string_2), .string_2(block_paint_12_string_2));  // open: shift_2
  S_R_Flip_Flop s_r_ff_7 (
    .Q(s_r_ff_7_q), .preset(rst), .reset(min_comparator_7_result), .en(clk));  // open: S, clk, R, Qn
  min_comparator min_comparator_7 (
    .first(min_comparator_6_first_2), .second(min_comparator_6_second_2), .result(min_comparator_7_result),
    .second_2(min_comparator_7_second_2), .first_2(min_comparator_7_first_2));
  block_paint block_paint_13 (
    .data(s_r_ff_7_q), .\string (block_paint_11_string_2), .t_string(chip), .shift(block_paint_11_shift_2),
    .shift_2(block_paint_13_shift_2), .t_string_2(block_paint_13_t_string_2),
    .string_2(block_paint_13_string_2));
  block_paint block_paint_14 (
    .data(s_r_ff_7_q), .\string (block_paint_12_string_2), .t_string(chip), .shift(block_paint_11_shift_2),
    .t_string_2(block_paint_14_t_string_2), .string_2(block_paint_14_string_2));  // open: shift_2
  S_R_Flip_Flop s_r_ff_8 (
    .Q(s_r_ff_8_q), .preset(rst), .reset(min_comparator_8_result), .en(clk));  // open: S, clk, R, Qn
  min_comparator min_comparator_8 (
    .first(min_comparator_7_first_2), .second(min_comparator_7_second_2), .result(min_comparator_8_result));  // open: second_2, first_2
  block_paint block_paint_15 (
    .data(s_r_ff_8_q), .\string (block_paint_13_string_2), .t_string(chip), .shift(block_paint_13_shift_2),
    .t_string_2(block_paint_15_t_string_2));  // open: shift_2, string_2
  block_paint block_paint_16 (
    .data(s_r_ff_8_q), .\string (block_paint_14_string_2), .t_string(chip), .shift(block_paint_13_shift_2),
    .t_string_2(block_paint_16_t_string_2));  // open: shift_2, string_2

  // Other names for the same wires on the sheet: ID2[4:0] = chip_ID
endmodule

module block_paint (
  input  data,
  input  [4:0] \string ,
  input  [4:0] t_string,
  input  [4:0] shift,
  output [31:0] t_string_2,
  output [4:0] string_2,
  output [4:0] shift_2
);

  wire comparator_1_eq;
  wire [4:1] pull_resistor_4_node;
  wire [31:0] decoder_32_inv_1_out, multiplexer_1_out, shifter_1_out, shifter_2_out, shifter_3_out;

  Pull_Resistor pull_resistor_1 (.node(pull_resistor_4_node[4]));
  Pull_Resistor pull_resistor_2 (.node(pull_resistor_4_node[3]));
  Pull_Resistor pull_resistor_3 (.node(pull_resistor_4_node[2]));
  Pull_Resistor pull_resistor_4 (.node(pull_resistor_4_node[1]));
  Comparator #(.width(5)) comparator_1 (
    .a({pull_resistor_4_node, data}), .b({5{1'b0}}), .eq(comparator_1_eq));  // open: gt, lt
  decoder_32_inv decoder_32_inv_1 (
    .data({pull_resistor_4_node, data}), .A(\string ), .B(t_string), .out(decoder_32_inv_1_out));
  Shifter #(.width(32), .shift("lr")) shifter_1 (.in(decoder_32_inv_1_out), .\dist (shift), .out(shifter_1_out));
  Adder #(.width(5)) adder_1 (.a(shift), .b(5'b00100), .out(shift_2));  // open: cin, cout
  Multiplexer #(.width(32)) multiplexer_1 (
    .in0(shifter_1_out), .in1({32{1'b0}}), .out(multiplexer_1_out), .sel(comparator_1_eq));  // open: en
  Shifter #(.width(32)) shifter_2 (.in(multiplexer_1_out), .\dist (5'b00010), .out(shifter_2_out));
  Shifter #(.width(32)) shifter_3 (.in(multiplexer_1_out), .\dist (5'b00001), .out(shifter_3_out));
  assign t_string_2 = multiplexer_1_out | shifter_2_out | shifter_3_out;  // OR_Gate or_1, 32 bits wide

  assign string_2 = \string ;
endmodule

module min_comparator (
  input  [5:0] first,
  input  [5:0] second,
  output [5:0] first_2,
  output result,
  output [5:0] second_2
);

  Comparator #(.width(6)) comparator_1 (.a(first), .b(second), .eq(result));  // open: gt, lt
  Adder #(.width(6)) adder_1 (.a(second), .b(6'b000001), .out(second_2));  // open: cin, cout

  assign first_2 = first;
endmodule

module blockID_calculation (
  input  [4:0] ballx,
  input  [4:0] bally,
  output [5:0] out_3
);

  wire [5:0] adder_1_out, bit_extender_1_out, bit_extender_2_out, divider_1_out, divider_2_out,
       multiplier_1_out, subtractor_1_out, subtractor_2_out;

  // Probe on bit_extender_1_out
  assign bit_extender_1_out = {{1{1'b0}}, ballx};  // Bit_Extender bit_extender_1
  // Probe on bit_extender_2_out
  assign bit_extender_2_out = {{1{1'b0}}, bally};  // Bit_Extender bit_extender_2
  Subtractor #(.width(6)) subtractor_1 (
    .a(bit_extender_1_out), .b(6'b000001), .out(subtractor_1_out));  // open: bin, bout
  Subtractor #(.width(6)) subtractor_2 (
    .a(bit_extender_2_out), .b(6'b000001), .out(subtractor_2_out));  // open: bin, bout
  Divider #(.width(6)) divider_1 (.a(subtractor_1_out), .b(6'b000100), .out(divider_1_out));  // open: upper, rem
  Divider #(.width(6)) divider_2 (.a(subtractor_2_out), .b(6'b000011), .out(divider_2_out));  // open: upper, rem
  Multiplier #(.width(6)) multiplier_1 (.a(6'b001000), .b(divider_2_out), .out(multiplier_1_out));  // open: cin, cout
  Adder #(.width(6)) adder_1 (.a(divider_1_out), .b(multiplier_1_out), .out(adder_1_out));  // open: cin, cout
  Adder #(.width(6)) adder_2 (.a(adder_1_out), .b(6'b000001), .out(out_3));  // open: cin, cout
endmodule

module triger_of_deleting (
  input  triger,
  input  [4:0] ballx,
  input  [4:0] bally,
  output [5:0] blockID
);

  wire [5:0] blockid_calculation_1_out_3;

  blockID_calculation blockid_calculation_1 (.ballx(ballx), .bally(bally), .out_3(blockid_calculation_1_out_3));
  Transistor #(.\type ("n"), .width(6)) transistor_1 (.in(blockid_calculation_1_out_3), .out(blockID), .gate(triger));
endmodule

module velocity_calculation (
  input  clock,
  input  vel_trig,
  output [15:0] velocity
);

  wire [2:0] random_1_out;
  wire [15:0] adder_1_out, bit_extender_1_out;

  Random #(.width(3)) random_1 (.clk(clock), .next(vel_trig), .out(random_1_out));  // open: clr
  assign bit_extender_1_out = {{13{1'b0}}, random_1_out};  // Bit_Extender bit_extender_1
  Adder #(.width(16)) adder_1 (.a(bit_extender_1_out), .b(16'h1), .out(adder_1_out));  // open: cin, cout
  Transistor #(.\type ("n"), .width(16)) transistor_1 (.in(adder_1_out), .out(velocity), .gate(vel_trig));

  // Other names for the same wires on the sheet: clk = clock
endmodule

module IO_adress_processing (
  input  [15:0] rd_in,
  input  [15:0] addr,
  input  [15:0] in,
  input  [15:0] out,
  input  rd,
  input  mem,
  input  word,
  input  [15:0] neededAddr,
  output trig_to_log,
  output trig_out_log,
  output [15:0] wr_out,
  output [15:0] addr_2,
  output [15:0] in_2,
  output [15:0] out_2,
  output rd_2,
  output mem_2,
  output word_2
);

  wire comparator_1_eq;

  Comparator #(.width(16), .mode("unsigned")) comparator_1 (
    .a(addr), .b(neededAddr), .eq(comparator_1_eq));  // open: gt, lt
  and and_1 (trig_to_log, comparator_1_eq, ~word, mem, ~rd);  // AND_Gate
  Multiplexer #(.width(16), .enable("false")) multiplexer_1 (.in0(in), .in1(rd_in), .out(in_2), .sel(trig_out_log));
  and and_2 (trig_out_log, comparator_1_eq, ~word, mem, rd);  // AND_Gate

  assign addr_2 = addr;
  assign mem_2 = mem;
  assign out_2 = out;
  assign rd_2 = rd;
  assign word_2 = word;
  assign wr_out = out;

  // Other names for the same wires on the sheet: out_log = trig_out_log
endmodule

module test (
  input  bus_0
);

  wire cdm_16_1_p1, cdm_16_2_p2, cdm_16_2_p3, cdm_16_2_p5, cdm_16_3_p2, cdm_16_3_p3, cdm_16_3_p5, clk,
       comparator_1_eq, comparator_2_eq, comparator_3_eq, comparator_4_eq, comparator_5_eq, comparator_6_eq,
       comparator_7_eq, comparator_8_eq, comparator_9_eq, io_adress_processing_1_mem_2,
       io_adress_processing_1_rd_2, io_adress_processing_1_word_2, io_adress_processing_2_mem_2,
       io_adress_processing_2_rd_2, io_adress_processing_2_word_2, io_adress_processing_3_mem_2,
       io_adress_processing_3_rd_2, io_adress_processing_3_word_2, io_adress_processing_4_mem_2,
       io_adress_processing_4_rd_2, io_adress_processing_4_word_2, mem, memMux, memMux1, memMux2, not_1_out,
       not_2_out, not_3_out, rd, rst, s_r_ff_1_q, s_r_ff_2_q, s_r_ff_3_q, tr1, tr2, triger, word;
  wire [2:0] cdm_16_2_p1, cdm_16_2_p4, cdm_16_3_p1, cdm_16_3_p4;
  wire [4:0] ballx, bally, multiplexer_2_out, multiplexer_6_out, x_joystick;
  wire [7:0] cdm_16_2_p1_2, cdm_16_2_p4_2, cdm_16_3_p1_2, cdm_16_3_p4_2, io_adress_processing_1_wr_out,
       io_adress_processing_1_wr_out_2, pull_resistor_3_node, score, transistor_4_out, transistor_6_out;
  wire [15:0] addr, bit_extender_1_out, bit_extender_2_out, cdm_16_1_p6, cdm_16_1_p7, cdm_16_2_p10,
       cdm_16_2_p11, cdm_16_3_p10, cdm_16_3_p11, controlled_buffer_2_out, controlled_buffer_4_out,
       controlled_buffer_5_out, data, io_adress_processing_1_addr_2, io_adress_processing_1_out_2,
       io_adress_processing_2_addr_2, io_adress_processing_2_in_2, io_adress_processing_2_out_2,
       io_adress_processing_3_addr_2, io_adress_processing_3_in_2, io_adress_processing_3_out_2,
       io_adress_processing_4_addr_2, io_adress_processing_4_in_2, io_adress_processing_4_out_2,
       io_adress_processing_5_in_2, io_adress_processing_5_out_2, kbdMemIn, kbdMemIn1, kbdMemIn2,
       multiplexer_4_out, multiplexer_5_out, velocity_calculation_1_velocity,
       velocity_calculation_2_velocity, velocity_calculation_3_velocity;

  // Debugger debugger_1: pin names not known
  // Debugger debugger_2: pin names not known
  // Probe on cdm_16_2_p2
  Comparator #(.width(5)) comparator_1 (.a({5{1'b1}}), .b(bally), .eq(comparator_1_eq));  // open: gt, lt
  // CdM_16 cdm_16_1: pin names not known; wires that end beside it: cdm_16_1_p1, mem, rd, word, addr, cdm_16_1_p6, cdm_16_1_p7
  S_R_Flip_Flop s_r_ff_1 (.Q(s_r_ff_1_q), .preset(rst), .reset(comparator_2_eq), .en(clk));  // open: S, clk, R, Qn
  Comparator #(.width(5)) comparator_2 (.a({5{1'b1}}), .b(bally), .eq(comparator_2_eq));  // open: gt, lt
  // CdM_16 cdm_16_2: pin names not known; wires that end beside it: {cdm_16_2_p1_2, ballx, cdm_16_2_p1}, cdm_16_2_p2, cdm_16_2_p3, {cdm_16_2_p4_2, bally, cdm_16_2_p4}, cdm_16_2_p5, mem, rd, word, addr, cdm_16_2_p10, cdm_16_2_p11
  Pull_Resistor pull_resistor_1 (.node(cdm_16_2_p3));
  Transistor #(.\type ("n")) transistor_1 (.in(clk), .out(cdm_16_2_p3), .gate(s_r_ff_2_q));
  S_R_Flip_Flop s_r_ff_2 (.Q(s_r_ff_2_q), .preset(rst), .reset(comparator_1_eq), .en(clk));  // open: S, clk, R, Qn
  Pull_Resistor pull_resistor_2 (.node(cdm_16_1_p1));
  Transistor #(.\type ("n")) transistor_2 (.in(clk), .out(cdm_16_1_p1), .gate(s_r_ff_1_q));
  // Probe on cdm_16_2_p5
  Multiplexer #(.width(16), .enable("false")) multiplexer_1 (
    .in0(controlled_buffer_2_out), .in1(kbdMemIn), .out(cdm_16_1_p7), .sel(memMux));
  Comparator #(.width(16)) comparator_3 (.a(addr), .b(16'hcccc), .eq(comparator_3_eq));  // open: gt, lt
  Register register_1 (.D(pull_resistor_3_node), .en(triger), .Q(score), .clk(clk), .clr(rst));
  Pull_Resistor pull_resistor_3 (.node(pull_resistor_3_node));
  Transistor #(.\type ("n"), .width(8)) transistor_3 (
    .in(io_adress_processing_1_wr_out), .out(pull_resistor_3_node), .gate(triger));
  IO_adress_processing io_adress_processing_1 (
    .addr(addr), .in_2(cdm_16_2_p11), .out(cdm_16_2_p10), .rd(rd), .mem(mem), .word(word),
    .addr_2(io_adress_processing_1_addr_2), .in(io_adress_processing_2_in_2),
    .out_2(io_adress_processing_1_out_2), .rd_2(io_adress_processing_1_rd_2),
    .mem_2(io_adress_processing_1_mem_2), .word_2(io_adress_processing_1_word_2), .trig_to_log(triger),
    .wr_out({io_adress_processing_1_wr_out_2, io_adress_processing_1_wr_out}), .neededAddr(16'hcccc));  // open: rd_in, trig_out_log
  Comparator #(.width(16)) comparator_4 (.a(addr), .b(16'hbeef), .eq(comparator_4_eq));  // open: gt, lt
  IO_adress_processing io_adress_processing_2 (
    .rd_in(bit_extender_1_out), .addr(io_adress_processing_1_addr_2), .in_2(io_adress_processing_2_in_2),
    .out(io_adress_processing_1_out_2), .rd(io_adress_processing_1_rd_2), .mem(io_adress_processing_1_mem_2),
    .word(io_adress_processing_1_word_2), .addr_2(io_adress_processing_2_addr_2),
    .in(io_adress_processing_3_in_2), .out_2(io_adress_processing_2_out_2),
    .rd_2(io_adress_processing_2_rd_2), .mem_2(io_adress_processing_2_mem_2),
    .word_2(io_adress_processing_2_word_2), .neededAddr(16'hbeef));  // open: trig_to_log, wr_out, trig_out_log
  velocity_calculation velocity_calculation_1 (.clock(clk), .vel_trig(tr1), .velocity(velocity_calculation_1_velocity));
  assign bit_extender_1_out = {{11{1'b0}}, x_joystick};  // Bit_Extender bit_extender_1
  assign data = not_1_out ? cdm_16_1_p6 : 16'bz;  // Controlled_Buffer controlled_buffer_1
  not not_1 (not_1_out, rd);
  assign controlled_buffer_2_out = rd ? data : 16'bz;  // Controlled_Buffer controlled_buffer_2
  and and_1 (triger, ~rd, mem, ~word, comparator_3_eq);  // AND_Gate
  IO_adress_processing io_adress_processing_3 (
    .rd_in(velocity_calculation_1_velocity), .addr(io_adress_processing_2_addr_2),
    .in_2(io_adress_processing_3_in_2), .out(io_adress_processing_2_out_2), .rd(io_adress_processing_2_rd_2),
    .mem(io_adress_processing_2_mem_2), .word(io_adress_processing_2_word_2),
    .addr_2(io_adress_processing_3_addr_2), .in(io_adress_processing_4_in_2),
    .out_2(io_adress_processing_3_out_2), .rd_2(io_adress_processing_3_rd_2),
    .mem_2(io_adress_processing_3_mem_2), .word_2(io_adress_processing_3_word_2), .trig_out_log(tr1),
    .neededAddr(16'ha000));  // open: trig_to_log, wr_out
  velocity_calculation velocity_calculation_2 (.clock(clk), .vel_trig(tr2), .velocity(velocity_calculation_2_velocity));
  Transistor #(.\type ("n"), .width(8)) transistor_4 (.in(cdm_16_1_p6[7:0]), .out(transistor_4_out), .gate(triger));
  and and_2 (memMux, rd, mem, ~word, comparator_4_eq);  // AND_Gate
  IO_adress_processing io_adress_processing_4 (
    .rd_in(velocity_calculation_2_velocity), .addr(io_adress_processing_3_addr_2),
    .in_2(io_adress_processing_4_in_2), .out(io_adress_processing_3_out_2), .rd(io_adress_processing_3_rd_2),
    .mem(io_adress_processing_3_mem_2), .word(io_adress_processing_3_word_2),
    .addr_2(io_adress_processing_4_addr_2), .in(io_adress_processing_5_in_2),
    .out_2(io_adress_processing_4_out_2), .rd_2(io_adress_processing_4_rd_2),
    .mem_2(io_adress_processing_4_mem_2), .word_2(io_adress_processing_4_word_2), .trig_out_log(tr2),
    .neededAddr(16'ha001));  // open: trig_to_log, wr_out
  assign bit_extender_2_out = {{15{1'b0}}, rst};  // Bit_Extender bit_extender_2
  Register register_2 (.D(transistor_4_out), .en(triger), .Q(score), .clk(clk), .clr(rst));
  Pull_Resistor pull_resistor_4 (.node(transistor_4_out));
  velocity_calculation velocity_calculation_3 (
    .clock(clk), .vel_trig(bus_0), .velocity(velocity_calculation_3_velocity));
  IO_adress_processing io_adress_processing_5 (
    .rd_in(bit_extender_2_out), .addr(io_adress_processing_4_addr_2), .in_2(io_adress_processing_5_in_2),
    .out(io_adress_processing_4_out_2), .rd(io_adress_processing_4_rd_2), .mem(io_adress_processing_4_mem_2),
    .word(io_adress_processing_4_word_2), .in(controlled_buffer_4_out), .out_2(io_adress_processing_5_out_2),
    .neededAddr(16'ha002));  // open: addr_2, rd_2, mem_2, word_2, trig_to_log, wr_out, trig_out_log
  Multiplexer #(.width(5), .enable("false")) multiplexer_2 (
    .in0({5{1'b0}}), .in1(x_joystick), .out(multiplexer_2_out), .sel(memMux));
  // Probe on velocity_calculation_3_velocity
  assign data = not_2_out ? io_adress_processing_5_out_2 : 16'bz;  // Controlled_Buffer controlled_buffer_3
  not not_2 (not_2_out, rd);
  assign controlled_buffer_4_out = rd ? data : 16'bz;  // Controlled_Buffer controlled_buffer_4
  assign kbdMemIn = {{11{1'b0}}, multiplexer_2_out};  // Bit_Extender bit_extender_3
  // RAM ram_1: pin names not known; wires that end beside it: addr, word, mem, clk, rd, data
  // RAM ram_2: pin names not known; wires that end beside it: addr, word, mem, clk, rd, data
  // Probe on cdm_16_3_p2
  // Debugger debugger_3: pin names not known
  // CdM_16 cdm_16_3: pin names not known; wires that end beside it: {cdm_16_3_p1_2, ballx, cdm_16_3_p1}, cdm_16_3_p2, cdm_16_3_p3, {cdm_16_3_p4_2, bally, cdm_16_3_p4}, cdm_16_3_p5, mem, rd, word, addr, cdm_16_3_p10, cdm_16_3_p11
  Pull_Resistor pull_resistor_5 (.node(cdm_16_3_p3));
  Transistor #(.\type ("n")) transistor_5 (.in(clk), .out(cdm_16_3_p3), .gate(s_r_ff_3_q));
  S_R_Flip_Flop s_r_ff_3 (.Q(s_r_ff_3_q), .preset(rst), .reset(comparator_5_eq), .en(clk));  // open: S, clk, R, Qn
  Comparator #(.width(5)) comparator_5 (.a({5{1'b1}}), .b(bally), .eq(comparator_5_eq));  // open: gt, lt
  // Probe on cdm_16_3_p5
  Multiplexer #(.width(16), .enable("false")) multiplexer_3 (
    .in0(multiplexer_4_out), .in1(kbdMemIn), .out(cdm_16_3_p11), .sel(memMux));
  Multiplexer #(.width(16), .enable("false")) multiplexer_4 (
    .in0(multiplexer_5_out), .in1(kbdMemIn1), .out(multiplexer_4_out), .sel(memMux1));
  Comparator #(.width(16)) comparator_6 (.a(addr), .b(16'hcccc), .eq(comparator_6_eq));  // open: gt, lt
  Register register_3 (.Q(score));  // open: D, en, clk, clr
  Multiplexer #(.width(16), .enable("false")) multiplexer_5 (
    .in0(controlled_buffer_5_out), .in1(kbdMemIn2), .out(multiplexer_5_out), .sel(memMux2));
  and and_3 (triger, ~rd, mem, ~word, comparator_6_eq);  // AND_Gate
  Comparator #(.width(16)) comparator_7 (.a(addr), .b(16'hbeef), .eq(comparator_7_eq));  // open: gt, lt
  Comparator #(.width(16)) comparator_8 (.a(addr), .b(16'ha000), .eq(comparator_8_eq));  // open: gt, lt
  Comparator #(.width(16)) comparator_9 (.a(addr), .b(16'ha001), .eq(comparator_9_eq));  // open: gt, lt
  and and_4 (memMux, rd, mem, ~word, comparator_7_eq);  // AND_Gate
  and and_5 (memMux1, rd, mem, ~word, comparator_8_eq);  // AND_Gate
  and and_6 (memMux2, rd, mem, ~word, comparator_9_eq);  // AND_Gate
  assign controlled_buffer_5_out = rd ? data : 16'bz;  // Controlled_Buffer controlled_buffer_5
  Transistor #(.\type ("n"), .width(8)) transistor_6 (.in(cdm_16_3_p10[7:0]), .out(transistor_6_out), .gate(triger));
  Pull_Resistor pull_resistor_6 (.node(transistor_6_out));
  velocity_calculation velocity_calculation_4 (.clock(clk));  // open: vel_trig, velocity
  assign data = not_3_out ? cdm_16_3_p10 : 16'bz;  // Controlled_Buffer controlled_buffer_6
  not not_3 (not_3_out, rd);
  Register register_4 (.D(transistor_6_out), .en(triger), .Q(score), .clk(clk), .clr(rst));
  velocity_calculation velocity_calculation_5 (.clock(clk), .vel_trig(memMux1), .velocity(kbdMemIn1));
  Multiplexer #(.width(5), .enable("false")) multiplexer_6 (
    .in0({5{1'b0}}), .in1(x_joystick), .out(multiplexer_6_out), .sel(memMux));
  velocity_calculation velocity_calculation_6 (.clock(clk), .vel_trig(memMux2), .velocity(kbdMemIn2));
  assign kbdMemIn = {{11{1'b0}}, multiplexer_6_out};  // Bit_Extender bit_extender_4
  // RAM ram_3: pin names not known; wires that end beside it: addr, word, mem, clk, rd, data
endmodule
